# Fritzing sketch Arduino Dual LFO (saved by Fritzing 0.9.3b)
circuit board: 14.9013cm x 7.84578cm
breadboards: 1

parts:
  C2 = Ceramic Capacitor [capacitance=100nF package="100 mil [THT, multilayer]"]
  S5 = Round Pushbutton [part_number="Wave (1)"]
  S6 = Round Pushbutton [part_number="Wave (2)"]
  R2 = Resistor [tolerance=±5% resistance=1k part_number="Lowpass (1)" package=THT]
  R8 = Rotary Potentiometer (Small) [maximum_resistance=10kΩ package=THT]
  R7 = Rotary Potentiometer (Small) [maximum_resistance=10kΩ package=THT]
  R6 = Rotary Potentiometer (Small) [maximum_resistance=10kΩ package=THT]
  R9 = Rotary Potentiometer (Small) [maximum_resistance=10kΩ package=THT]
  C1 = Ceramic Capacitor [capacitance=100nF package="100 mil [THT, multilayer]"]
  R1 = Resistor [tolerance=±5% resistance=1k part_number="Lowpass (2)" package=THT]
  Part1 = Arduino Uno (Rev3)

nets:
  LFO (2): C2.0, R2.Pin_1
  GND: C2.1, S5.leg1, S6.leg1, R8.leg1, R7.leg1, R6.leg1, R9.leg1, C1.1, Part1.GND
  Wave Switch (1): S5.leg0, Part1.D10_PWM/SS
  Wave Switch (2): S6.leg0, Part1.D12/MISO
  PWM Output (2): R2.Pin_0, Part1.D3_PWM
  Frequency (2): R8.wiper, Part1.A1
  5V: R8.leg2, R7.leg2, R6.leg2, R9.leg2, Part1.5V
  Depth (1): R7.wiper, Part1.A4/SDA
  Frequency (1): R6.wiper, Part1.A0
  Depth (2): R9.wiper, Part1.A5/SCL
  LFO (1): C1.0, R1.Pin_1
  PWM Output (1): R1.Pin_0, Part1.D11_PWM/MOSI
  Trigger 1: Part1.D4
  Trigger 2: Part1.D6_PWM

notes:
  LFO (1)
  WAVEFORM SELECTOR SWITCH
  FREQUENCY POT
  DEPTH POT
  LFO (2)
  WAVEFORM SELECTOR SWITCH
  FREQUENCY POT
  DEPTH POT
  LFO 2 OUT:
  LFO 1 OUT:
  Trigger 2
  Trigger 1
